# Fritzing sketch schroedingers-dice (saved by Fritzing 0.9.6b)

parts:
  Bauteil1 = Arduino Nano (Rev3.0) (ICSP)
  Bauteil2 = LCD1602-I2C
  S5 = Pushbutton [package="[THT]"]
  S6 = Pushbutton [package="[THT]"]
  S7 = Pushbutton [package="[THT]"]
  VCC2 = Battery
  VCC3 = Battery
  S8 = Taiway 100-SP-X-T1 SPDT Miniature Toggle Switch [part_number=100-SP-X-T1-0-0-B1-M2 package=THT]
  R1 = Resistor [tolerance=±1% resistance=1k package="0603 [SMD]"]
  R2 = Resistor [tolerance=±1% resistance=1k package="0603 [SMD]"]
  J1 = male pin header, 3 pins [form="♂ (male)"]
  S9 = Pushbutton [package="[THT]"]

nets:
  5V: Bauteil1.D1/TX, Bauteil1.5V, Bauteil2.VCC, J1.pin1
  GND: Bauteil1.GND, Bauteil1.D3, Bauteil1.D4, Bauteil2.GND, S5.Pin_1, S5.Pin_2, S5.Pin_3, S5.Pin_4, S6.Pin_1, S6.Pin_3, S6.Pin_4, S7.Pin_3, S7.Pin_4, VCC2.-, R2.Pin_0, J1.pin2, S9.Pin_4
  N1: Bauteil1.D2, J1.pin3
  N2: Bauteil1.D5, S7.Pin_1, S7.Pin_2
  N3: Bauteil1.D6, S9.Pin_1, S9.Pin_2
  N4: Bauteil1.VIN, S8.L2
  N5: Bauteil1.A5, Bauteil2.SCL
  N6: Bauteil1.A4, Bauteil2.SDA
  N7: Bauteil1.A2, R1.Pin_1, R2.Pin_1
  N8: VCC2.+, VCC3.-
  N9: VCC3.+, S8.L1, R1.Pin_0

notes:
  LCD display
  geiger counter
  voltage divider
  Arduiono Nano
  On/Off
  yellow button
  green button
  blue button
  red button
  lamp/LED if wanted

custom parts:
  LCD1602-I2C: A standard character display, usually with 2x16 characters. Comes in many colors with LCM1602 IIC attached.
